// Logisim project l2.circ as structural Verilog: 5 circuits, main circuit calculadorafisica
module Calculadoralogica (
  input  clk,
  input  num0,
  input  num1,
  input  num2,
  input  num3,
  input  num4,
  input  num5,
  input  num6,
  input  num7,
  input  num8,
  input  num9,
  input  changevar,
  input  resetvar,
  input  toaddition,
  input  tosubtration,
  input  ToDivide10,
  output var1,
  output isadd,
  output var2,
  output issub,
  output [3:0] result_5,
  output [3:0] op2val_5,
  output [3:0] op1val_5,
  output [3:0] result_4,
  output [3:0] op2val_4,
  output [3:0] op1val_4,
  output [3:0] result_3,
  output [3:0] op2val_3,
  output [3:0] op1val_3,
  output [3:0] result_2,
  output [3:0] op2val_2,
  output [3:0] op1val_2,
  output [3:0] result_1,
  output [3:0] op2val_1,
  output [3:0] op1val_1
);

  wire adder_1_cout, currentop_tipo, currentoperando, not_1_out, or_1_out, or_2_out, or_3_out, or_4_out,
       or_5_out, regcurrent_tipo, regcurrentop, state_click_1_isdown, state_click_2_isdown,
       state_click_3_isdown, subtractor_1_bout;
  wire [15:0] adder_1_out, controlled_buffer_1_out, controlled_buffer_11_out, controlled_buffer_15_out,
       controlled_buffer_16_out, currentopval, demultiplexer_4_out0, demultiplexer_4_out1, divider_1_out,
       multiplexer_2_out, multiplexer_3_out, op1_newval, op1val, op2_newval, op2val, result, resultop,
       subtractor_1_out;

  assign controlled_buffer_1_out = num0 ? {16{1'b0}} : 16'bz;  // Controlled_Buffer controlled_buffer_1
  assign controlled_buffer_1_out = num1 ? 16'h1 : 16'bz;  // Controlled_Buffer controlled_buffer_2
  assign controlled_buffer_1_out = num2 ? 16'h2 : 16'bz;  // Controlled_Buffer controlled_buffer_3
  assign controlled_buffer_1_out = num3 ? 16'h3 : 16'bz;  // Controlled_Buffer controlled_buffer_4
  assign controlled_buffer_1_out = num4 ? 16'h4 : 16'bz;  // Controlled_Buffer controlled_buffer_5
  assign controlled_buffer_1_out = num5 ? 16'h5 : 16'bz;  // Controlled_Buffer controlled_buffer_6
  assign controlled_buffer_1_out = num6 ? 16'h6 : 16'bz;  // Controlled_Buffer controlled_buffer_7
  assign controlled_buffer_1_out = num7 ? 16'h7 : 16'bz;  // Controlled_Buffer controlled_buffer_8
  assign controlled_buffer_1_out = num8 ? 16'h8 : 16'bz;  // Controlled_Buffer controlled_buffer_9
  assign controlled_buffer_1_out = num9 ? 16'h9 : 16'bz;  // Controlled_Buffer controlled_buffer_10
  Demultiplexer #(.width(16), .tristate("true"), .enable("false")) demultiplexer_1 (
    .out0(op1_newval), .out1(op2_newval), .in(controlled_buffer_11_out), .sel(regcurrentop));
  assign controlled_buffer_11_out = resetvar ? {16{1'b0}} : 16'bz;  // Controlled_Buffer controlled_buffer_11
  state_click state_click_1 (.clk(clk), .currentvalue(changevar), .IsDown(state_click_1_isdown));  // open: Value
  assign currentop_tipo = toaddition ? 1'b0 : 1'bz;  // Controlled_Buffer controlled_buffer_12
  assign currentop_tipo = tosubtration ? 1'b1 : 1'bz;  // Controlled_Buffer controlled_buffer_13
  or or_1 (or_1_out, num0, num1, num2);
  or or_2 (or_2_out, num3, num4, num5);
  or or_3 (or_3_out, or_1_out, or_2_out, or_4_out);
  or or_4 (or_4_out, num6, num7, num8);
  not not_1 (not_1_out, regcurrentop);
  Divider #(.width(16)) divider_1 (.a(currentopval), .b(16'ha), .out(divider_1_out));  // open: upper, rem
  state_click state_click_2 (.clk(clk), .currentvalue(ToDivide10), .IsDown(state_click_2_isdown));  // open: Value
  or or_5 (or_5_out, or_3_out, num9);
  assign currentoperando = state_click_1_isdown ? not_1_out : 1'bz;  // Controlled_Buffer controlled_buffer_14
  assign controlled_buffer_15_out = state_click_2_isdown ? divider_1_out : 16'bz;  // Controlled_Buffer controlled_buffer_15
  Demultiplexer #(.width(16), .tristate("true"), .enable("false")) demultiplexer_2 (
    .out0(op1_newval), .out1(op2_newval), .in(controlled_buffer_15_out), .sel(regcurrentop));
  Demultiplexer #(.enable("false")) demultiplexer_3 (.out0(var1), .out1(var2), .in(1'b1), .sel(regcurrentop));
  assign controlled_buffer_16_out = state_click_3_isdown ? controlled_buffer_1_out : 16'bz;  // Controlled_Buffer controlled_buffer_16
  state_click state_click_3 (.clk(clk), .currentvalue(or_5_out), .IsDown(state_click_3_isdown));  // open: Value
  Demultiplexer #(.width(16), .tristate("true"), .enable("false")) demultiplexer_4 (
    .out0(demultiplexer_4_out0), .out1(demultiplexer_4_out1), .in(controlled_buffer_16_out),
    .sel(regcurrentop));
  Demultiplexer #(.enable("false")) demultiplexer_5 (.out0(isadd), .out1(issub), .in(1'b1), .sel(regcurrent_tipo));
  Register #(.width(16)) R0 (.D(op1_newval), .Q(op1val), .clk(clk));  // open: en, clr
  adddezena16 adddezena16_1 (.Value(op1val), .ValueAdd(demultiplexer_4_out0), .CurrentValue(op1_newval));
  adddezena16 adddezena16_2 (.Value(op2val), .ValueAdd(demultiplexer_4_out1), .CurrentValue(op2_newval));
  Register #(.width(16)) R1 (.D(op2_newval), .Q(op2val), .clk(clk));  // open: en, clr
  decimal16 decimal16_1 (
    .Val(op1val), .out_2(op1val_5), .out_3(op1val_4), .out_4(op1val_3), .out_5(op1val_2), .out_6(op1val_1));
  Multiplexer #(.width(16), .enable("false")) multiplexer_1 (
    .in0(op1val), .in1(op2val), .out(currentopval), .sel(regcurrentop));
  Subtractor #(.width(16)) subtractor_1 (
    .a(op1val), .b(op2val), .out(subtractor_1_out), .bout(subtractor_1_bout));  // open: bin
  decimal16 decimal16_2 (
    .Val(op2val), .out_2(op2val_5), .out_3(op2val_4), .out_4(op2val_3), .out_5(op2val_2), .out_6(op2val_1));
  Register #(.width(16)) RS (.D(resultop), .Q(result), .clk(clk));  // open: en, clr
  Adder #(.width(16)) adder_1 (.a(op1val), .b(op2val), .out(adder_1_out), .cout(adder_1_cout));  // open: cin
  Multiplexer #(.width(16), .enable("false")) multiplexer_2 (
    .in0(adder_1_out), .in1({16{1'b1}}), .out(multiplexer_2_out), .sel(adder_1_cout));
  Multiplexer #(.width(16), .enable("false")) multiplexer_3 (
    .in0(subtractor_1_out), .in1({16{1'b0}}), .out(multiplexer_3_out), .sel(subtractor_1_bout));
  Multiplexer #(.width(16), .enable("false")) multiplexer_4 (
    .in0(multiplexer_2_out), .in1(multiplexer_3_out), .out(resultop), .sel(regcurrent_tipo));
  decimal16 decimal16_3 (
    .Val(result), .out_2(result_5), .out_3(result_4), .out_4(result_3), .out_5(result_2), .out_6(result_1));
  D_Flip_Flop d_ff_1 (.clk(clk), .D(currentoperando), .Q(regcurrentop));  // open: Qn, preset, en, reset
  D_Flip_Flop d_ff_2 (.clk(clk), .D(currentop_tipo), .Q(regcurrent_tipo));  // open: Qn, preset, en, reset

  // Other names for the same wires on the sheet: button1 = num0; button2 = num1; button3 = num2; button4 = num3;
  //   button5 = num4; button6 = num5; button7 = num6; button8 = num7; button9 = num8; button10 = num9;
  //   op1 = changevar; op_mais = toaddition; op_menos = tosubtration; reset = resetvar
endmodule

module state_click (
  input  clk,
  input  currentvalue,
  output IsDown,
  output Value
);

  wire and_1_out, value_qn;

  D_Flip_Flop u_value (.clk(clk), .D(currentvalue), .Q(Value), .Qn(value_qn));  // open: preset, en, reset
  and and_1 (and_1_out, value_qn, currentvalue);
  D_Flip_Flop u_isdown (.clk(clk), .D(and_1_out), .Q(IsDown));  // open: Qn, preset, en, reset
endmodule

module calculadorafisica (
);

  wire A, B, C, clock_1_out, D, D1, D2, E, E1, E2, F, G, H, I, J, K, L, M, N, T;
  wire [3:0] A1, A2, A3, A4, A5, B1, B2, B3, B4, B5, C1, C2, C3, C4, C5;

  Button _0 (.out(A));
  Button _3 (.out(D));
  Button _6 (.out(G));
  Button _9 (.out(J));
  Button button (.out(M));
  Button _2 (.out(C));
  Button _1 (.out(B));
  Button _5 (.out(F));
  Button _4 (.out(E));
  Button _8 (.out(I));
  Button _7 (.out(H));
  Button R (.out(L));
  Button u_E (.out(K));
  Button X (.out(T));
  Button button_2 (.out(N));
  LED led_1 (.in(D1));
  LED led_2 (.in(D2));
  Clock clock_1 (.out(clock_1_out));
  Hex_Digit_Display hex_digit_display_1 (.value(C4));  // open: dp
  Hex_Digit_Display hex_digit_display_2 (.value(C5));  // open: dp
  Hex_Digit_Display hex_digit_display_3 (.value(B4));  // open: dp
  Hex_Digit_Display hex_digit_display_4 (.value(B5));  // open: dp
  Hex_Digit_Display hex_digit_display_5 (.value(A5));  // open: dp
  Hex_Digit_Display hex_digit_display_6 (.value(A4));  // open: dp
  Calculadoralogica calculadoralogica_1 (
    .clk(clock_1_out), .num0(A), .num1(B), .num2(C), .num3(D), .num4(E), .num5(F), .num6(G), .num7(H),
    .num8(I), .num9(J), .changevar(K), .resetvar(L), .toaddition(M), .tosubtration(N), .op1val_3(C3),
    .op2val_3(B3), .result_3(A3), .op1val_2(C2), .op2val_2(B2), .result_2(A2), .op1val_1(C1), .op2val_1(B1),
    .result_1(A1), .var1(D1), .isadd(E1), .var2(D2), .issub(E2), .op1val_4(C4), .op1val_5(C5), .op2val_5(B5),
    .op2val_4(B4), .result_4(A4), .result_5(A5), .ToDivide10(T));
  Hex_Digit_Display hex_digit_display_7 (.value(C3));  // open: dp
  Hex_Digit_Display hex_digit_display_8 (.value(C2));  // open: dp
  Hex_Digit_Display hex_digit_display_9 (.value(B2));  // open: dp
  Hex_Digit_Display hex_digit_display_10 (.value(B3));  // open: dp
  Hex_Digit_Display hex_digit_display_11 (.value(A2));  // open: dp
  Hex_Digit_Display hex_digit_display_12 (.value(A3));  // open: dp
  Hex_Digit_Display hex_digit_display_13 (.value(C1));  // open: dp
  Hex_Digit_Display hex_digit_display_14 (.value(B1));  // open: dp
  Hex_Digit_Display hex_digit_display_15 (.value(A1));  // open: dp
  LED led_3 (.in(E1));
  LED led_4 (.in(E2));

  // Notes on the sheet:
  //   +
  //   -
endmodule

module decimal16 (
  input  [15:0] Val,
  output [3:0] out_2,
  output [3:0] out_3,
  output [3:0] out_4,
  output [3:0] out_5,
  output [3:0] out_6
);

  wire [15:0] divider_1_rem, divider_2_rem, divider_3_rem;
  wire [15:4] divider_1_out, divider_2_out, divider_3_out, divider_4_out, divider_4_rem;

  Divider #(.width(16)) divider_1 (
    .a(Val), .b(16'h2710), .out({divider_1_out, out_2}), .rem(divider_1_rem));  // open: upper
  Divider #(.width(16)) divider_2 (
    .a(divider_1_rem), .b(16'h3e8), .out({divider_2_out, out_3}), .rem(divider_2_rem));  // open: upper
  Divider #(.width(16)) divider_3 (
    .a(divider_2_rem), .b(16'h64), .out({divider_3_out, out_4}), .rem(divider_3_rem));  // open: upper
  Divider #(.width(16)) divider_4 (
    .a(divider_3_rem), .b(16'ha), .out({divider_4_out, out_5}), .rem({divider_4_rem, out_6}));  // open: upper
endmodule

module adddezena16 (
  input  [15:0] Value,
  input  [15:0] ValueAdd,
  output [15:0] CurrentValue
);

  wire [15:0] multiplier_1_out;

  Multiplier #(.width(16)) multiplier_1 (.a(Value), .b(16'ha), .out(multiplier_1_out));  // open: cin, cout
  Adder #(.width(16)) adder_1 (.a(multiplier_1_out), .b(ValueAdd), .out(CurrentValue));  // open: cin, cout
endmodule
